# Fritzing sketch 7 segment led (saved by Fritzing 0.9.3b)
breadboards: 1

parts:
  U1 = 7-SEGMENT-DISPLAY [package=7-segment-display]
  R1 = Resistor [tolerance=±5% resistance=330 package=THT]
  R2 = Resistor [tolerance=±5% resistance=330 package=THT]
  R3 = Resistor [tolerance=±5% resistance=330 package=THT]
  R4 = Resistor [tolerance=±5% resistance=330 package=THT]
  R5 = Resistor [tolerance=±5% resistance=330 package=THT]
  R6 = Resistor [tolerance=±5% resistance=330 package=THT]
  R9 = Resistor [tolerance=±5% resistance=330 package=THT]
  U2 = 74HC595 SMD [package="SO16 [SMD]"]  # not connected
  Part1 = Arduino Ethernet Shield (Rev3)

nets:
  N1: U1.E, R3.Pin_0
  N2: U1.D, R4.Pin_0
  N3: U1.G1, R5.Pin_0
  N4: U1.C, Part1.5V
  N5: U1.DP, R6.Pin_0
  N6: U1.A, R1.Pin_0
  N7: U1.G2, R9.Pin_0
  N8: U1.G, R2.Pin_0
